// Logisim project ControlUnit.circ as structural Verilog: 1 circuit, main circuit ControlUnit
module ControlUnit (
  input  [5:0] in_1,
  input  [5:0] in_2,
  output out_3,
  output out_4,
  output out_5,
  output out_6,
  output out_7,
  output out_8,
  output out_9,
  output [3:0] out_10
);

  wire [1:0] main_decoder_1_aluop_1_0;

  Main_Decoder main_decoder_1 (
    .MemtoReg(out_4), .MemWrite(out_5), .Branch(out_6), .ALUSrc(out_7), .RegDst(out_8), .RegWrite(out_9),
    .Jump(out_3), .ALUOp_1_0(main_decoder_1_aluop_1_0), .Opcode_5_0(in_1));
  ALU_Decoder alu_decoder_1 (.ALUOp_1_0(main_decoder_1_aluop_1_0), .ALUCtrl_3_0(out_10), .Funct_5_0(in_2));
endmodule
